# Fritzing sketch 4th Chebyshev Filter TLE2426LP ケース内配線 (saved by Fritzing 0.9.2b)
perfboards: 1

parts:
  J1 = female pin header, 2 pins [form="♀ (female)"]
  J2 = female pin header, 3 pins [form="♀ (female)"]
  J3 = female pin header, 2 pins [form="♀ (female)"]
  TRS1 = Audio Jack (TRS) 3.5mm [package="4Ucon 08780 [THT]"]
  TRS2 = Audio Jack (TRS) 3.5mm [package="4Ucon 08780 [THT]"]
  S1 = Toggle Switch [package=THT]
  R1 = Rotary Potentiometer (Small) [maximum_resistance=100kΩ package=THT]
  S2 = Toggle Switch [package=THT]
  VCC1 = Battery block 9V
  Power_plug1 = Power plug
  S3 = Toggle Switch [package=THT]

nets:
  N1: J1.pin1, TRS1.Sleeve, R1.leg1
  N2: J1.pin2, R1.wiper
  N3: J2.pin1, TRS2.Sleeve
  N4: J2.pin2, TRS2.Ring
  N5: J2.pin3, TRS2.Tip
  N6: J3.pin1, S2.COM
  N7: J3.pin2, S3.COM
  N8: TRS1.Ring, S1.L2
  N9: TRS1.Tip, S1.L1
  N10: S1.COM, R1.leg2
  N11: S2.L2, VCC1.+, Power_plug1.GND
  N12: Power_plug1.VCC, S3.L1

notes:
  IN
  OUT
  G/Filtered/Bypass
  PWR
  PWR Plug
  w / SW
