# Fritzing sketch Chebyshev 4th LPF (saved by Fritzing 0.9.2b)
breadboards: 1

parts:
  IC1 = Dual Op-Amp [package=dip08]
  C1 = Ceramic Capacitor [capacitance=100nF package="100 mil [THT, multilayer]"]
  R1 = Resistor [tolerance=±5% resistance=2.7k package=THT]
  R2 = Resistor [tolerance=±5% resistance=6.8k package=THT]
  C2 = Ceramic Capacitor [capacitance=100nF package="100 mil [THT, multilayer]"]
  R3 = Resistor [tolerance=±5% resistance=2.7k package=THT]
  C3 = Ceramic Capacitor [capacitance=100nF package="100 mil [THT, multilayer]"]
  R4 = Resistor [tolerance=±5% resistance=7.5k package=THT]
  R5 = Resistor [tolerance=±5% resistance=13k package=THT]
  C4 = Ceramic Capacitor [capacitance=100nF package="100 mil [THT, multilayer]"]
  R6 = Resistor [tolerance=±5% resistance=7.5k package=THT]
  C5 = Ceramic Capacitor [capacitance=100nF package="100 mil [THT, multilayer]"]
  C6 = Ceramic Capacitor [capacitance=100nF package="100 mil [THT, multilayer]"]
  R7 = Rotary Potentiometer (Small) [maximum_resistance=100kΩ package=THT]

nets:
  N1: IC1.A_OUT, C1.1, R1.Pin_1, R6.Pin_0
  N2: IC1.A_-IN, C1.0, R2.Pin_1
  N3: IC1.A_+IN, IC1.B_+IN, C2.0, C4.1, C5.1, C6.1, R7.leg1
  N4: IC1.A_V-, C5.0
  N5: IC1.B_-IN, C3.1, R5.Pin_1
  N6: IC1.B_OUT, C3.0, R4.Pin_1
  N7: IC1.A_V+, C6.0
  N8: R1.Pin_0, R2.Pin_0, C2.1, R3.Pin_1
  N9: R3.Pin_0, R7.wiper
  N10: R4.Pin_0, R5.Pin_0, C4.0, R6.Pin_1

notes:
  IN
  OUT
  V-
  GND
  GND
  V+
